// Logisim project ProjectElevator.circ as structural Verilog: 1 circuit, main circuit main
module main (
  input  [3:0] DF,
  input  [3:0] CF,
  input  RESET,
  output a2,
  output a1,
  output a0,
  output A,
  output Q0,
  output F1,
  output F3,
  output B,
  output b2,
  output b3,
  output b0,
  output b1,
  output c2,
  output C,
  output F4,
  output c3,
  output c0,
  output c1,
  output D,
  output d1,
  output d3,
  output F5,
  output d0,
  output d2,
  output Q1,
  output F2,
  output e3,
  output E,
  output e2,
  output e1,
  output e0,
  output J,
  output j0,
  output j1,
  output j2,
  output j3
);

  wire CLK_out, not_8_out, not_9_out;

  Clock CLK (.out(CLK_out));
  Comparator #(.width(4)) comparator_1 (.a(DF), .b(CF), .gt(a1), .eq(b2), .lt(b3));
  not not_1 (b0, a0);
  not not_2 (c2, a1);
  not not_3 (c1, a2);
  not not_4 (d3, b3);
  not not_5 (d0, a0);
  not not_6 (e2, a1);
  not not_7 (j1, a2);
  nand nand_1 (A, a0, a1, a2);
  or or_1 (B, b3, b2, a2, b0);
  or or_2 (C, b2, c2, c1, a0);
  or or_3 (D, d3, b2, a2, d0);
  nand nand_2 (E, b3, e2, a2, a0);
  or or_4 (J, a1, a0, j1, b2);
  and and_1 (F1, A, B, C);
  and and_2 (F2, D, E, J);
  D_Flip_Flop u_D1 (.clk(CLK_out), .D(F1), .Q(a2), .preset(RESET));  // open: Qn, en, reset
  D_Flip_Flop u_D2 (.clk(CLK_out), .D(F2), .Q(a0), .preset(RESET));  // open: Qn, en, reset
  not not_8 (not_8_out, a2);
  not not_9 (not_9_out, a0);
  and and_3 (F3, not_8_out, a0);
  LED led_1 (.in(F3));
  and and_4 (F4, not_9_out, a2);
  LED led_2 (.in(F4));
  and and_5 (F5, a2, a0);
  LED led_3 (.in(F5));

  assign b1 = a2;
  assign c0 = a0;
  assign c3 = b2;
  assign d1 = a2;
  assign d2 = b2;
  assign e0 = a2;
  assign e1 = a0;
  assign e3 = b3;
  assign j0 = b2;
  assign j2 = a0;
  assign j3 = a1;
  assign Q0 = a2;
  assign Q1 = a0;

  // Notes on the sheet:
  //   DESTINATED FLOOR
  //   CURRENT FLOOR
  //   UP
  //   DOWN
  //   STOP/DOOR OPEN
endmodule
